# Fritzing sketch Fritzing Elemanları (saved by Fritzing 1.0.2b)
circuit board: 8.46667cm x 5.64444cm
breadboards: 1

parts:
  Onderdeel1 = Arduino Uno (Rev3)  # not connected
  LCM1602_IIC1 = LCM1602 IIC [part_number="LCM1602 IIC" chip_label="LCM1602 IIC" package="DIP (Dual Inline) [THT]"]
  LCD1 = LCD screen
  Parça1 = Arduino Nano (Rev3.0)
  DHT1 = DHT11 Humitidy and Temperature Sensor
  R1 = Resistor [tolerance=±5% power=0.25W resistance=10k package=THT]
  IC1 = MQ-2 [part_number=1 package="DIP (Dual Inline) [THT]"]  # not connected
  J1 = Basic Servo  # not connected
  S1 = H-Bridge with L298N
  M1 = DC Motor [voltage_(max)=6V voltage_(min)=3V]

nets:
  VSS: LCM1602_IIC1.VSS, LCD1.VSS
  VDD: LCM1602_IIC1.VDD, LCD1.VDD
  N1: LCM1602_IIC1.V0, LCD1.V0
  N2: LCM1602_IIC1.RS, LCD1.RS
  N3: LCM1602_IIC1.RW, LCD1.R/W
  N4: LCM1602_IIC1.E, LCD1.E
  N5: LCM1602_IIC1.D0, LCD1.DB0
  N6: LCM1602_IIC1.D1, LCD1.DB1
  N7: LCM1602_IIC1.D2, LCD1.DB2
  N8: LCM1602_IIC1.D3, LCD1.DB3
  N9: LCM1602_IIC1.D4, LCD1.DB4
  N10: LCM1602_IIC1.D5, LCD1.DB5
  N11: LCM1602_IIC1.D6, LCD1.DB6
  N12: LCM1602_IIC1.D7, LCD1.DB7
  N13: LCM1602_IIC1.A, LCD1.LED+
  N14: LCM1602_IIC1.K, LCD1.LED-
  N15: LCM1602_IIC1.LED_A, LCM1602_IIC1.LED_B
  GND: Parça1.GND, DHT1.GND
  N16: Parça1.D2, DHT1.DATA, R1.Pin_1
  N17: DHT1.VDD, R1.Pin_0
  N18: S1.M1-01, M1.pin_2
  N19: S1.M1-02, M1.pin_1

notes:
  DHT 11 PİN SIRALAMASI
  SOLDAN -> 1.VCC 2.DATA 3.N/C 4.GND
  MQ SERİCİ SENSÖRLERİN PİN SIRALAMASI
  SOLDAN-> 1.VCC 2.GND 3.D0 4.A0
  D0-> DİJİTAL ÇIKIŞ
  A0-> ANALOG ÇIKIŞ
  İ2C LCD MODÜL PİN SIRALAMASI
  i2c --> Arduino
  SCL --> A5
  SDA --> A4
  VCC --> 5V
  GND --> GND
  SERVO MOTOR PİN SIRALAMASI
  SARI - > SİNYAL,
  KIRMIZI->5V,
  SİYAH->GND
  L298 DC MOTOR SÜRÜCÜ BAĞLANTISI
  L298 --> Arduino
  ENA --> D9
  IN1 --> D8
  IN2 --> D7
  Öğr. Gör. Ali ÇETİNKAYA https://github.com/acetinkaya/ https://alicetinkaya.site/

custom parts:
  LCM1602 IIC: I2C-Module to use a 1602 or 2004 LCD on with the wire.h libory Serial LCD Modul
  DHT11 Humitidy and Temperature Sensor: DHT11 Humidity and Temperature Sensor
  MQ-2: MQ-2 Gas Sensor module
  H-Bridge with L298N: h-bridge

// code stored in the sketch: AnalogReadSerial2LCD_LED.ino
#include <Wire.h>
#include <LiquidCrystal_I2C.h>

LiquidCrystal_I2C lcd(0x27, 16, 2);   // adress and format LCD

const int analogInPin = A0;           // Analog input pin that the potentiometer is attached to
const int analogOutPin = 9;           // Analog output pin that the LED is attached to

int sensorValue = 0;                  // value read from the pot
int outputValue = 0;                  // value output to the PWM (analog out)

void setup() {
  lcd.init();                         // init LCD
  lcd.backlight();
  lcd.home();
  lcd.setCursor(5, 0);                // place static text
  lcd.print("ADC = ");
  lcd.setCursor(15, 0);
  lcd.print("V");
  lcd.setCursor(0, 1);
  lcd.print("LED : ");
  lcd.setCursor(12, 1);
  lcd.print("%");
  Serial.begin(9600);                 // optional serial monitor
}

void loop() {
  int sensorValue = analogRead(analogInPin);          // read analog A0 en store in sensorValue
  float voltValue = 5.0 / 1024.0 * sensorValue;       // calculate volt at analog A0 and store in voltValue
  float percentValue = sensorValue / 1024.0 * 100.0;  // calculate percentage analog A0 and store in percentValue
  outputValue = map(sensorValue, 0, 1023, 0, 255);    // map analog input to analog output and store in outputValue
  analogWrite(analogOutPin, outputValue);             // write outputValue to analogOutPin

  lcd.setCursor(0, 0);                                // set cursor at deserid position
  leadingZeros(sensorValue, 4);                       // print sensorvalue with number of leading-characters (0 or space as specified in function leadingZeros)
  lcd.setCursor(10, 0);                               // set cursor at deserid position
  lcd.print(voltValue);                               // print voltValue
  lcd.setCursor(6, 1);                                // set cursor at deserid position
  lcd.print(percentValue);                            // print percentValue

  Serial.print("sensor = " );                         // print the results to the serial monitor:
  Serial.print(sensorValue);
  Serial.print("\t output = ");
  Serial.print(outputValue);
  Serial.print("\t procent = ");
  Serial.println(percentValue);

  delay(1000);                                        // set delay
}

void leadingZeros( int value, int width) {            // display result with leading characters
  char valueStr[6];                                   // large enough to hold an int
  itoa (value, valueStr, 10);                         // itoa converts int to string
  int len = strlen(valueStr);                         // calculate length of valueStr
  if (len < width) {
    len = width - len;
    while (len--)
      lcd.print(' ');                                 // for leading zeros place '0' between (), for leading spaces place ' ' between ()
  }
  lcd.print(valueStr);
}
